# Fritzing sketch circuitoMain (saved by Fritzing 0.9.3b)
circuit board: 13.2539cm x 10.6983cm
breadboards: 12

parts:
  U1 = 74HC595 [package="DIP16 [THT]"]
  U2 = 74HC595 [package="DIP16 [THT]"]
  U3 = 74HC595 [package="DIP16 [THT]"]
  U4 = 74HC595 [package="DIP16 [THT]"]
  U5 = 74HC595 [package="DIP16 [THT]"]
  U6 = 74HC595 [package="DIP16 [THT]"]
  U8 = 74HC595 [package="DIP16 [THT]"]
  Q9 = Basic FET P-Channel [package="TO220 [THT]"]  # not connected
  Q10 = Basic FET P-Channel [package="TO220 [THT]"]
  Q11 = Basic FET P-Channel [package="TO220 [THT]"]
  Q12 = Basic FET P-Channel [package="TO220 [THT]"]
  Q13 = Basic FET P-Channel [package="TO220 [THT]"]
  Q14 = Basic FET P-Channel [package="TO220 [THT]"]
  Q15 = Basic FET P-Channel [package="TO220 [THT]"]
  Q16 = Basic FET P-Channel [package="TO220 [THT]"]
  Q17 = Basic FET P-Channel [package="TO220 [THT]"]
  Q18 = Basic FET P-Channel [package="TO220 [THT]"]
  Q19 = Basic FET P-Channel [package="TO220 [THT]"]
  Q20 = Basic FET P-Channel [package="TO220 [THT]"]
  Q21 = Basic FET P-Channel [package="TO220 [THT]"]
  Q22 = Basic FET P-Channel [package="TO220 [THT]"]
  Q23 = Basic FET P-Channel [package="TO220 [THT]"]
  Q24 = Basic FET P-Channel [package="TO220 [THT]"]
  Q34 = Basic FET P-Channel [package="TO220 [THT]"]
  Q35 = Basic FET P-Channel [package="TO220 [THT]"]
  Q36 = Basic FET P-Channel [package="TO220 [THT]"]
  Q37 = Basic FET P-Channel [package="TO220 [THT]"]
  Q38 = Basic FET P-Channel [package="TO220 [THT]"]
  Q39 = Basic FET P-Channel [package="TO220 [THT]"]
  Q40 = Basic FET P-Channel [package="TO220 [THT]"]
  Q41 = Basic FET P-Channel [package="TO220 [THT]"]
  Q42 = Basic FET P-Channel [package="TO220 [THT]"]
  Q43 = Basic FET P-Channel [package="TO220 [THT]"]
  Q44 = Basic FET P-Channel [package="TO220 [THT]"]
  Q45 = Basic FET P-Channel [package="TO220 [THT]"]
  Q46 = Basic FET P-Channel [package="TO220 [THT]"]
  Q47 = Basic FET P-Channel [package="TO220 [THT]"]
  Q48 = Basic FET P-Channel [package="TO220 [THT]"]
  Q49 = Basic FET P-Channel [package="TO220 [THT]"]
  Q50 = Basic FET P-Channel [package="TO220 [THT]"]
  Q51 = Basic FET P-Channel [package="TO220 [THT]"]
  Q52 = Basic FET P-Channel [package="TO220 [THT]"]
  Q53 = Basic FET P-Channel [package="TO220 [THT]"]
  Q54 = Basic FET P-Channel [package="TO220 [THT]"]
  Q55 = Basic FET P-Channel [package="TO220 [THT]"]
  Q56 = Basic FET P-Channel [package="TO220 [THT]"]
  Q57 = Basic FET P-Channel [package="TO220 [THT]"]
  Q58 = Basic FET P-Channel [package="TO220 [THT]"]
  Q59 = Basic FET P-Channel [package="TO220 [THT]"]
  Q60 = Basic FET P-Channel [package="TO220 [THT]"]
  Q61 = Basic FET P-Channel [package="TO220 [THT]"]
  Q62 = Basic FET P-Channel [package="TO220 [THT]"]
  Q63 = Basic FET P-Channel [package="TO220 [THT]"]
  Q64 = Basic FET P-Channel [package="TO220 [THT]"]
  Q65 = Basic FET P-Channel [package="TO220 [THT]"]
  Q66 = Basic FET P-Channel [package="TO220 [THT]"]
  Q67 = Basic FET P-Channel [package="TO220 [THT]"]
  Q68 = Basic FET P-Channel [package="TO220 [THT]"]
  Q69 = Basic FET P-Channel [package="TO220 [THT]"]
  Q70 = Basic FET P-Channel [package="TO220 [THT]"]
  Q71 = Basic FET P-Channel [package="TO220 [THT]"]
  Q72 = Basic FET P-Channel [package="TO220 [THT]"]
  Q73 = Basic FET P-Channel [package="TO220 [THT]"]

nets:
  N1: U1.Q3, U1.DS, U2.Q7, Q16.gate
  N2: U1.Q4, U1.OE, Q72.gate
  N3: U1.Q5, Q70.gate
  N4: U1.Q6, U1.SH_CP, Q73.gate
  N5: U1.Q7, U2.SH_CP, U3.SH_CP, U4.SH_CP, U5.Q7, U6.SH_CP, U8.Q7
  GND: U1.GND, U2.GND, U2.OE, U3.OE, U4.OE, U5.GND, U6.GND, U6.OE, U8.GND, Q10.source, Q11.source, Q12.source, Q13.source, Q14.source, Q16.source, Q17.source, Q19.source, Q20.source, Q21.source, Q22.source, Q23.source, Q24.source, Q34.source, Q35.source, Q36.source, Q37.source, Q38.source, Q39.source, Q40.source, Q42.source, Q43.source, Q45.source, Q46.source, Q47.source, Q48.source, Q49.source, Q50.source, Q51.source, Q52.source, Q53.source, Q54.source, Q55.source, Q56.source, Q57.source, Q58.source, Q59.source, Q60.source, Q61.source, Q62.source, Q63.source, Q64.source, Q65.source, Q66.source, Q67.source, Q68.source, Q69.source, Q71.source, Q72.source, Q73.source
  N6: U1.Q7', U2.DS
  N7: U1.MR, Q69.gate
  N8: U2.Q1, Q10.gate
  N9: U2.Q2, Q11.gate
  N10: U2.Q3, Q12.gate
  N11: U2.Q4, Q13.gate
  N12: U2.Q5, Q14.gate
  N13: U2.Q6, Q15.gate
  N14: U2.Q7', U3.DS
  VCC: U2.MR, U2.VCC, U3.MR, U3.VCC, U4.MR, U4.VCC, U6.MR, U6.VCC
  N15: U2.ST_CP, U3.ST_CP, U4.ST_CP, U6.ST_CP
  N16: U3.Q1, Q17.gate
  N17: U3.Q2, Q23.gate
  N18: U3.Q3, Q24.gate
  N19: U3.Q4, Q18.gate
  N20: U3.Q5, Q19.gate
  N21: U3.Q6, Q22.gate
  N22: U3.Q7, Q21.gate
  N23: U3.Q0, Q20.gate, Q20.drain
  N24: U4.Q1, Q56.gate
  N25: U4.Q2, Q52.gate
  N26: U4.Q3, Q51.gate
  N27: U4.Q4, Q57.gate
  N28: U4.Q5, Q55.gate
  N29: U4.Q6, Q50.gate
  N30: U4.Q7, Q53.gate
  N31: U4.DS, U6.Q7'
  N32: U4.Q0, Q54.gate
  N33: U5.Q3, U5.DS, U6.Q7, Q45.gate
  N34: U5.Q4, U5.OE, Q40.gate
  N35: U5.Q5, Q38.gate
  N36: U5.Q6, U5.SH_CP, Q41.gate
  N37: U5.Q7', U6.DS
  N38: U5.MR, Q37.gate
  N39: U6.Q1, Q48.gate
  N40: U6.Q2, Q44.gate
  N41: U6.Q3, Q43.gate
  N42: U6.Q4, Q49.gate
  N43: U6.Q5, Q47.gate
  N44: U6.Q6, Q42.gate
  N45: U6.Q0, Q46.gate
  N46: U8.Q3, U8.DS
  N47: U8.Q4, U8.OE, Q64.gate, Q64.drain
  N48: U8.Q5, Q62.gate
  N49: U8.Q6, U8.SH_CP, Q65.gate
  N50: U8.MR, Q61.gate
